// Logisim project Traffic_light_gen1.circ as structural Verilog: 2 circuits, main circuit main
module main (
);

  wire clock_1_out, counter_to_light_1_u1, counter_to_light_1_u2, counter_to_light_1_u3, j_k_ff_1_q,
       j_k_ff_2_q, j_k_ff_3_q, not_1_out, not_2_out;

  Clock clock_1 (.out(clock_1_out));
  J_K_Flip_Flop j_k_ff_1 (.J(1'b1), .clk(clock_1_out), .K(1'b1), .Q(j_k_ff_1_q));  // open: Qn, preset, en, reset
  not not_1 (not_1_out, j_k_ff_1_q);
  J_K_Flip_Flop j_k_ff_2 (.J(1'b1), .clk(not_1_out), .K(1'b1), .Q(j_k_ff_2_q));  // open: Qn, preset, en, reset
  not not_2 (not_2_out, j_k_ff_2_q);
  J_K_Flip_Flop j_k_ff_3 (.J(1'b1), .clk(not_2_out), .K(1'b1), .Q(j_k_ff_3_q));  // open: Qn, preset, en, reset
  Counter_to_light counter_to_light_1 (
    .a1(j_k_ff_3_q), .a2(j_k_ff_2_q), .a3(j_k_ff_1_q), .u1(counter_to_light_1_u1),
    .u2(counter_to_light_1_u2), .u3(counter_to_light_1_u3));
  LED led_1 (.in(counter_to_light_1_u3));
  LED led_2 (.in(counter_to_light_1_u2));
  LED led_3 (.in(counter_to_light_1_u1));
endmodule

module Counter_to_light (
  input  a1,
  input  a2,
  input  a3,
  output u1,
  output u2,
  output u3
);

  wire and_1_out, and_2_out, not_1_out, not_2_out;

  and and_1 (and_1_out, a1, a3);
  and and_2 (and_2_out, a1, a2);
  not not_1 (not_1_out, a2);
  not not_2 (not_2_out, a3);
  not not_3 (u3, a1);
  or or_1 (u1, and_1_out, and_2_out);
  and and_3 (u2, a1, not_1_out, not_2_out);
endmodule
